# Fritzing sketch TMP102 (saved by Fritzing 0.8.6b)
breadboards: 1

parts:
  U1 = Spark Core (v1.0)
  Part1 = Digital Temperature Sensor Breakout - TMP102

nets:
  N1: U1.A2, U1.3V3, Part1.V+
  N2: U1.A3, U1.A6
  N3: U1.A5, U1.VIN
  GND: U1.GND, Part1.GND, Part1.ADD0
  N4: U1.D0, Part1.SDA
  N5: U1.D1, Part1.SCL

custom parts:
  Spark Core (v1.0): The Spark Core is a tiny Wi-Fi development board that makes it easy to create internet-connected hardware. The Core is all you need to get started; power it over USB and in minutes you'll be controlling LEDs, switches and motors and collecting data from sensors over the internet! It has 8 digital I/O pins, 8 analog I/O pins, 8 PWM pins; UART (Serial), SPI, I2C, and JTAG peripherals available.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
