# Fritzing sketch TMP36 (saved by Fritzing 0.8.6b)
circuit board: 2.81638cm x 3.84764cm
breadboards: 1

parts:
  U2 = TMP36 Temperature Sensor [package="TO92 [THT]"]
  C1 = Ceramic Capacitor [capacitance=100nF package="100 mil [THT, multilayer]"]
  U1 = Spark Core (v1.0)
  part = Ceramic Capacitor [capacitance=100nF package="100 mil [THT, multilayer]"]  # not connected

nets:
  N1: U2.+Vs, U1.3V3*
  A7: U2.Vout, C1.0, U1.A7
  GND: U2.GND, C1.1, U1.GND
  N2: U1.A2, U1.3V3
  N3: U1.A3, U1.A6
  N4: U1.A5, U1.VIN

custom parts:
  Spark Core (v1.0): The Spark Core is a tiny Wi-Fi development board that makes it easy to create internet-connected hardware. The Core is all you need to get started; power it over USB and in minutes you'll be controlling LEDs, switches and motors and collecting data from sensors over the internet! It has 8 digital I/O pins, 8 analog I/O pins, 8 PWM pins; UART (Serial), SPI, I2C, and JTAG peripherals available.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
